// Logisim project smips.circ as structural Verilog
module Board (
);

  wire CLK, HALT, MEM_WE, RESET, TTY_WE;
  wire [3:0] MEM_BE;
  wire [6:0] TTY_DATA;
  wire [31:0] MEM_ADDR, MEM_RDATA, MEM_WDATA;

  Clock Reloj (.out(CLK));
  Button u_Reset (.out(RESET));
  CPU cpu_1 (
    .CLK(CLK), .RESET(RESET), .MEM_RDATA(MEM_RDATA), .MEM_ADDR(MEM_ADDR), .MEM_WDATA(MEM_WDATA),
    .MEM_BE(MEM_BE), .MEM_WE(MEM_WE), .TTY_DATA(TTY_DATA), .TTY_WE(TTY_WE), .HALT(HALT));
  TTY #(.cols(48), .rows(12)) tty_1 (.data(TTY_DATA), .clk(CLK), .we(TTY_WE), .clr(RESET));
  Memory memory_1 (.CLK(CLK), .ADDR(MEM_ADDR), .WDATA(MEM_WDATA), .BE(MEM_BE), .WE(MEM_WE), .RDATA(MEM_RDATA));
  LED u_Halt (.in(HALT));

  // Notes on the sheet:
  //   S-MIPS | Board
  //   No modificar: la CPU se implementa dentro del subcircuito CPU.
endmodule

module CPU (
  input  CLK,
  input  [31:0] MEM_ADDR,
  input  RESET,
  input  [31:0] MEM_WDATA,
  input  [31:0] MEM_RDATA,
  input  [3:0] MEM_BE,
  input  MEM_WE,
  input  [6:0] TTY_DATA,
  input  TTY_WE,
  input  HALT
);

  wire instruction_decoder_1_out_3, instruction_decoder_1_out_4, instruction_decoder_1_out_5,
       instruction_decoder_1_out_6, instruction_decoder_1_out_7, instruction_decoder_1_out_8,
       instruction_decoder_1_out_10, instruction_decoder_1_out_11, IsBeq, IsBne, IsBranch, undriven, ZeroF;
  wire [5:0] Funct, Op;

  Instruction_Decoder instruction_decoder_1 (
    .in_1(Op), .in_2(Funct), .out_3(instruction_decoder_1_out_3), .out_4(instruction_decoder_1_out_4),
    .out_5(instruction_decoder_1_out_5), .out_6(instruction_decoder_1_out_6),
    .out_7(instruction_decoder_1_out_7), .out_8(instruction_decoder_1_out_8), .out_9(HALT),
    .out_10(instruction_decoder_1_out_10), .out_11(instruction_decoder_1_out_11));
  FSM fsm_1 (
    .in_1(CLK), .in_3(instruction_decoder_1_out_3), .in_4(instruction_decoder_1_out_4),
    .in_5(instruction_decoder_1_out_5), .in_6(instruction_decoder_1_out_10),
    .in_7(instruction_decoder_1_out_11), .in_8(instruction_decoder_1_out_6),
    .in_9(instruction_decoder_1_out_7), .in_10(instruction_decoder_1_out_8), .in_11(HALT));  // open: in_2, out_12, out_13, out_14, out_15, out_16, out_17, out_18, out_19, out_20, out_21, out_22, out_23, out_24, out_25, out_26
  Datapath datapath_1 (
    .out_17(Op), .out_19(Funct), .out_18(ZeroF));  // open: in_12, in_16, in_1, in_2, in_4, in_6, in_8, in_10, in_14, in_11, in_13, in_15, in_3, in_5, in_7, in_9
  BranchControl branchcontrol_1 (
    .in_1(IsBranch), .in_2(IsBeq), .in_3(IsBne), .in_4(ZeroF), .in_5(undriven));  // open: out_6

  // Other names for the same wires on the sheet: Illegal = HALT

  // Notes on the sheet:
  //   CPU S-MIPS: implementar aqui
  //   No cambiar nombres, anchos ni sentido de los pines: la placa depende de ellos.
endmodule

module Memory (
  input  CLK,
  input  [31:0] RDATA,
  input  [31:0] ADDR,
  input  [31:0] WDATA,
  input  [3:0] BE,
  input  WE
);

  RAM #(.addrWidth(12), .dataWidth(32)) ram_1 (
    .addr(ADDR[13:2]), .we(WE), .oe(1'b1), .clk(CLK), .din(WDATA), .dout(RDATA));

  // Other names for the same wires on the sheet: A[11:0] = ADDR[13:2]

  // Notes on the sheet:
  //   Memoria unificada: 4096 palabras de 32 bits (16 KiB), little-endian
  //   Lectura combinacional; escritura en el flanco de subida de CLK con WE=1, solo en los bytes con BE=1.
  //   Se usan los bits 13..2 de ADDR; los demas se ignoran (el espacio se repite cada 16 KiB).
endmodule

module ALU (
  input  [2:0] in_1,
  input  [31:0] in_2,
  input  [31:0] in_3,
  input  in_4,
  output [31:0] out_5,
  output ZeroF
);

  wire comparator_1_lt;
  wire [31:0] ADD, AND, COMP_SIGNED, LOGICAL_LEFT, LOGICAL_RIGHT, MINUS, OR;

  // Probe on in_2
  // Probe on in_2
  Adder #(.width(32)) adder_1 (.a(in_2), .b(in_3), .out(ADD));  // open: cin, cout
  Subtractor #(.width(32)) subtractor_1 (.a(in_2), .b(in_3), .out(MINUS));  // open: bin, bout
  Comparator #(.width(32)) comparator_1 (.a(in_2), .b(in_3), .lt(comparator_1_lt));  // open: gt, eq
  Shifter #(.shift("lr"), .width(32)) shifter_1 (.in(in_2), .\dist (in_3[4:0]), .out(LOGICAL_LEFT));
  Shifter #(.shift("lr"), .width(32)) shifter_2 (.in(in_2), .\dist (in_3[4:0]), .out(LOGICAL_RIGHT));
  // Probe on in_3
  // Probe on in_3
  assign AND = in_2 & in_3;  // AND_Gate and_1, 32 bits wide
  assign OR = in_2 | in_3;  // OR_Gate or_1, 32 bits wide
  assign COMP_SIGNED = {{31{comparator_1_lt}}, comparator_1_lt};  // Bit_Extender bit_extender_1
  // Probe on in_1
  // Probe on out_5
  // Probe on out_5
  Multiplexer #(.enable("true"), .select(3), .width(32)) multiplexer_1 (
    .in0(ADD), .in1(MINUS), .in2(AND), .in3(OR), .in4(COMP_SIGNED), .in5(LOGICAL_LEFT), .in6(LOGICAL_RIGHT),
    .in7(in_3), .out(out_5), .sel(in_1));  // open: en
  Comparator #(.width(32)) comparator_2 (.a({32{1'b0}}), .b(out_5), .eq(ZeroF));  // open: gt, lt

  // Other names for the same wires on the sheet: A[31:0] = in_2; B[31:0] = in_3; CLK = in_4; MAIN[31:0] = out_5;
  //   OP[2:0] = in_1; ZERO = ZeroF

  // Notes on the sheet:
  //   000
  //   001
  //   010
  //   011
  //   100
  //   0101
  //   110
  //   INPUTS
  //   OUTPUTS
  //   COMBINATIONAL LOGIC
endmodule

module Decoder (
  input  [1:0] ALUop,
  input  [5:0] FUNCT,
  output [2:0] OP
);

  ROM #(.dataWidth(3)) rom_1 (.addr({FUNCT, ALUop}), .data(OP));

  // Notes on the sheet:
  //   contents of rom_1 (hex, n*v repeats v):
  //   64*0 64*1 5 0 6 31*0 1 0 2 3 4*0 4
endmodule

module Datapath (
  input  in_1,
  input  in_2,
  input  in_3,
  input  in_4,
  input  in_5,
  input  in_6,
  input  in_7,
  input  in_8,
  input  in_9,
  input  [1:0] in_10,
  input  in_11,
  input  in_12,
  input  in_13,
  input  [3:0] in_14,
  input  in_15,
  input  [1:0] in_16,
  output [5:0] out_17,
  output out_18,
  output [5:0] out_19
);

  wire [2:0] ALUOP;
  wire [4:0] wa;
  wire [15:6] Inm;
  wire [25:16] IR;
  wire [31:0] A, ALUOUT, B, InA, InB, IorD_out, MDR, PCOUT, RALU, rd1, rd2, RDATA, sign_ext, wd;

  Register #(.width(32)) PC (.D(ALUOUT), .en(in_3), .clk(in_1), .Q(PCOUT));  // open: clr
  Register #(.width(32)) u_IR (.D(RDATA), .en(in_7), .clk(in_1), .Q({out_17, IR, Inm, out_19}));  // open: clr
  Register #(.width(32)) u_A (.D(rd1), .en(in_9), .clk(in_1), .Q(A));  // open: clr
  Register #(.width(32)) u_B (.D(rd2), .en(in_11), .clk(in_1), .Q(B));  // open: clr
  Decoder decoder_1 (.ALUop(in_16), .FUNCT(out_19), .OP(ALUOP));
  assign sign_ext = {{16{Inm[15]}}, {Inm, out_19}};  // Bit_Extender bit_extender_1
  Register #(.width(32)) u_ALUOUT (.D(ALUOUT), .en(in_15), .clk(in_1), .Q(RALU));  // open: clr
  Register #(.width(32)) u_MDR (.D(RDATA), .en(in_13), .clk(in_1), .Q(MDR));  // open: clr
  ALU alu_1 (.in_2(InA), .in_3(InB), .in_4(in_1), .in_1(ALUOP), .out_5(ALUOUT), .ZeroF(out_18));
  Multiplexer #(.width(5)) multiplexer_1 (.in0(IR[20:16]), .in1(Inm[15:11]), .out(wa), .sel(in_4));
  Multiplexer #(.width(32)) multiplexer_2 (.in0(PCOUT), .in1(ALUOUT), .out(IorD_out), .sel(in_2));
  Multiplexer #(.width(32)) multiplexer_3 (.in0(RALU), .in1(MDR), .out(wd), .sel(in_6));
  register_file register_file_1 (
    .clk(in_1), .we(in_5), .wa(wa), .wd(wd), .ra1(IR[25:21]), .ra2(IR[20:16]), .rd1(rd1), .rd2(rd2));  // open: rst
  Multiplexer #(.width(32)) multiplexer_4 (.in0(PCOUT), .in1(A), .out(InA), .sel(in_8));
  Multiplexer #(.select(2), .width(32)) multiplexer_5 (
    .in0(B), .in1(32'h100), .in2(sign_ext), .out(InB), .sel(in_10));  // open: in3
  Memory memory_1 (.CLK(in_1), .ADDR(IorD_out), .WDATA(B), .BE(in_14), .WE(in_12), .RDATA(RDATA));

  // Other names for the same wires on the sheet: ALUSrcA = in_8; ALUSrcB[1:0] = in_10; ALUwr = in_15; Awr = in_9;
  //   BE[3:0] = in_14; Bwr = in_11; clk = in_1; InOp[1:0] = in_16; IorD = in_2; funct[5:0] = out_19;
  //   Inm[5:0] = out_19; IR (some bits) = {out_17, Inm, out_19}; rd[4:0] = Inm[15:11]; rt[4:0] = IR[20:16];
  //   rs[4:0] = IR[25:21]; op[5:0] = out_17; IRwr = in_7; MDRwr = in_13; MemToReg = in_6; MemWrite = in_12;
  //   PCwr = in_3; RegDst = in_4; Regwr = in_5; ZeroF = out_18

  // Notes on the sheet:
  //   Direcciones
  //   Funct
  //   rd
  //   rt
  //   rs
  //   op
  //   INPUTS
  //   Reg Helpers
  //   ALU
  //   DECODER
  //   SIGN EXTENSION
  //   OUTPUTS
  //   REG FILE
  //   MUX Helpers
  //   MEMORY
endmodule

module BranchControl (
  input  in_1,
  input  in_2,
  input  in_3,
  input  in_4,
  input  in_5,
  output out_6
);

  wire and_1_out, and_2_out, not_1_out, or_1_out;

  and and_1 (and_1_out, in_2, in_4);
  and and_2 (and_2_out, in_3, not_1_out);
  not not_1 (not_1_out, in_4);
  or or_1 (or_1_out, and_1_out, and_2_out);
  and and_3 (out_6, or_1_out, in_5);

  // Other names for the same wires on the sheet: beq = in_2; bne = in_3; IsBranch = in_1; Pcwr = in_5; WE = out_6;
  //   ZeroF = in_4

  // Notes on the sheet:
  //   INPUTS
  //   OUTPUTS
  //   Combinational Logic
endmodule

module FSM (
  input  in_1,
  input  in_2,
  input  in_3,
  input  in_4,
  input  in_5,
  input  in_6,
  input  in_7,
  input  in_8,
  input  in_9,
  input  in_10,
  input  in_11,
  output out_12,
  output out_13,
  output out_14,
  output out_15,
  output out_16,
  output out_17,
  output out_18,
  output out_19,
  output out_20,
  output out_21,
  output out_22,
  output [1:0] out_23,
  output out_24,
  output out_25,
  output [1:0] out_26
);

  wire and_2_out, and_3_out, and_4_out, and_5_out, and_6_out, and_8_out, D0, D1, D2, D3, not_1_out, or_8_out,
       or_9_out, or_11_out, S1, S2, S9, S10, S11, S12, S13, S14, S15;
  wire [3:0] Qstate;

  Decoder_part #(.select(4)) decoder_1 (
    .out0(out_13), .out1(S1), .out2(S2), .out3(out_18), .out4(out_21), .out5(out_24), .out6(out_26[1]),
    .out7(out_20), .out8(out_25), .out9(S9), .out10(S10), .out11(S11), .out12(S12), .out13(S13), .out14(S14),
    .out15(S15), .sel(Qstate));  // open: en
  or or_1 (out_12, out_13, S9);
  or or_2 (out_17, out_13, S2);
  or or_3 (out_22, S2, out_26[1], out_25);
  or or_4 (out_23[0], out_13, S1);
  or or_5 (out_23[1], S1, S2);
  not not_1 (not_1_out, in_11);
  Register #(.width(4)) register_1 (.D({D3, D2, D1, D0}), .clk(in_1), .Q(Qstate), .clr(in_2));  // open: en
  and and_1 (out_15, S1, not_1_out);
  // Probe on Qstate
  or or_6 (out_14, out_21, out_20);
  or or_7 (out_19, out_18, out_24);
  or or_8 (or_8_out, in_6, in_8, in_7);
  and and_2 (and_2_out, S1, in_3);
  and and_3 (and_3_out, S2, in_5);
  or or_9 (or_9_out, in_5, in_4);
  and and_4 (and_4_out, S1, in_3);
  and and_5 (and_5_out, S1, in_8);
  and and_6 (and_6_out, S2, in_4);
  and and_7 (D3, S1, or_8_out);
  or or_10 (D2, out_18, and_2_out, and_3_out, out_26[1]);
  and and_8 (and_8_out, or_9_out, S1);
  or or_11 (or_11_out, out_26[1], and_4_out);
  or or_12 (D0, out_13, S2, out_26[1], and_5_out);
  or or_13 (D1, and_8_out, and_6_out, or_11_out);

  assign out_16 = out_15;
  assign out_26[0] = out_25;

  // Other names for the same wires on the sheet: ALUOP[1:0] = {out_26[1], out_25}; PCwrCond = out_25; S8 = out_25;
  //   S6 = out_26[1]; ALUSrcA = out_22; ALUSrcB[1:0] = out_23; ALUwr = out_17; Awr = out_15; Bwr = out_15; CLK = in_1;
  //   Dstate[3:0] = {D3, D2, D1, D0}; Illegal = in_11; IorD = out_19; IsBeq = in_6; IsBne = in_7; IsImm = in_9;
  //   IsJ = in_8; IsLoad = in_4; IsR = in_3; IsStore = in_5; IsSyscall = in_10; PCwr = out_12; Regwr = out_14;
  //   RST = in_2; IRwr = out_13; S0 = out_13; MDRwr = out_18; S3 = out_18; MemToReg = out_21; S4 = out_21;
  //   MemWrite = out_24; S5 = out_24; RegDst = out_20; S7 = out_20

  // Notes on the sheet:
  //   INPUTS
  //   OUTPUTS
  //   StateReg
  //   OUTPUT LOGIC
  //   NEXT STATE LOGIC
endmodule

module Instruction_Decoder (
  input  [5:0] in_1,
  input  [5:0] in_2,
  output out_3,
  output out_4,
  output out_5,
  output out_6,
  output out_7,
  output out_8,
  output out_9,
  output out_10,
  output out_11
);

  wire addi, andi, comparator_8_eq, comparator_17_eq, IsBranch, IsJ, IsJal, IsJr, IsLB, IsLBU, IsLW, IsSB,
       IsSW, lui, or_6_out, ori, stli;

  Comparator #(.width(6)) comparator_1 (.a(in_1), .b({6{1'b0}}), .eq(out_3));  // open: gt, lt
  Comparator #(.width(6)) comparator_2 (.a(in_1), .b(6'b000100), .eq(out_10));  // open: gt, lt
  Comparator #(.width(6)) comparator_3 (.a(in_1), .b(6'b000101), .eq(out_11));  // open: gt, lt
  Comparator #(.width(6)) comparator_4 (.a(in_1), .b(6'b100011), .eq(IsLW));  // open: gt, lt
  Comparator #(.width(6)) comparator_5 (.a(in_1), .b(6'b101011), .eq(IsSW));  // open: gt, lt
  Comparator #(.width(6)) comparator_6 (.a(in_1), .b(6'b000010), .eq(IsJ));  // open: gt, lt
  Comparator #(.width(6)) comparator_7 (.a(in_1), .b(6'b000011), .eq(IsJal));  // open: gt, lt
  Comparator #(.width(6)) comparator_8 (.a(in_2), .b(6'b001000), .eq(comparator_8_eq));  // open: gt, lt
  Comparator #(.width(6)) comparator_9 (.a(in_1), .b(6'b100000), .eq(IsLB));  // open: gt, lt
  Comparator #(.width(6)) comparator_10 (.a(in_1), .b(6'b100100), .eq(IsLBU));  // open: gt, lt
  Comparator #(.width(6)) comparator_11 (.a(in_1), .b(6'b101000), .eq(IsSB));  // open: gt, lt
  Comparator #(.width(6)) comparator_12 (.a(in_1), .b(6'b001000), .eq(addi));  // open: gt, lt
  Comparator #(.width(6)) comparator_13 (.a(in_1), .b(6'b001010), .eq(stli));  // open: gt, lt
  Comparator #(.width(6)) comparator_14 (.a(in_1), .b(6'b001100), .eq(andi));  // open: gt, lt
  Comparator #(.width(6)) comparator_15 (.a(in_1), .b(6'b001101), .eq(ori));  // open: gt, lt
  Comparator #(.width(6)) comparator_16 (.a(in_1), .b(6'b001111), .eq(lui));  // open: gt, lt
  and and_1 (IsJr, comparator_8_eq, out_3);
  or or_1 (IsBranch, out_10, out_11);
  Comparator #(.width(6)) comparator_17 (.a(in_2), .b(6'b001100), .eq(comparator_17_eq));  // open: gt, lt
  or or_2 (out_6, IsJ, IsJal, IsJr);
  or or_3 (out_4, IsLW, IsLB, IsLBU);
  or or_4 (out_5, IsSW, IsSB);
  or or_5 (out_7, addi, stli, andi, ori, lui);
  and and_2 (out_8, comparator_17_eq, out_3);
  or or_6 (or_6_out, IsBranch, out_6, out_4, out_3, out_8, out_7, out_5);
  not not_1 (out_9, or_6_out);

  // Other names for the same wires on the sheet: funct[5:0] = in_2; Illegal = out_9; IsBeq = out_10; IsBne = out_11;
  //   IsImm = out_7; IsJump = out_6; IsLoad = out_4; IsR = out_3; IsStore = out_5; IsSyscall = out_8; OP[5:0] = in_1

  // Notes on the sheet:
  //   INPUTS
  //   OUTPUTS
  //   Combinatoric Logic
endmodule

// VHDL entity register_file, as the project stores it:
library ieee;
use ieee.std_logic_1164.all;
use ieee.numeric_std.all;
entity register_file is
    port (
        clk   : in  std_logic;
        rst   : in  std_logic;
        we    : in  std_logic;                      -- Write Enable
        wa    : in  std_logic_vector(4 downto 0);   -- Write Address (rd / rt)
        wd    : in  std_logic_vector(31 downto 0);  -- Write Data
        ra1   : in  std_logic_vector(4 downto 0);   -- Read Address 1 (rs)
        ra2   : in  std_logic_vector(4 downto 0);   -- Read Address 2 (rt)
        rd1   : out std_logic_vector(31 downto 0);  -- Read Data 1
        rd2   : out std_logic_vector(31 downto 0)   -- Read Data 2
    );
end entity register_file;

architecture rtl of register_file is
    -- Definición del banco de 32 registros de 32 bits
    type reg_array is array (0 to 31) of std_logic_vector(31 downto 0);
    signal regs : reg_array;
begin

    -- Puerto de lectura 1 (Combinacional / Asíncrono)
    -- Si la dirección es 0 ($zero), retorna siempre 0.
    process(ra1, regs)
    begin
        if to_integer(unsigned(ra1)) = 0 then
            rd1 <= (others => '0');
        else
            rd1 <= regs(to_integer(unsigned(ra1)));
        end if;
    end process;

    -- Puerto de lectura 2 (Combinacional / Asíncrono)
    -- Si la dirección es 0 ($zero), retorna siempre 0.
    process(ra2, regs)
    begin
        if to_integer(unsigned(ra2)) = 0 then
            rd2 <= (others => '0');
        else
            rd2 <= regs(to_integer(unsigned(ra2)));
        end if;
    end process;

    -- Puerto de escritura (Síncrono al flanco de subida del reloj)
    process(clk)
    begin
        if rising_edge(clk) then
            if rst = '1' then
                -- Inicialización por reset según especificación [R6]
                for i in 0 to 31 loop
                    regs(i) <= (others => '0');
                end loop;
                regs(28) <= x"00001800"; -- $gp inicial = 0x1800[span_5](start_span)[span_5](end_span)[span_6](start_span)[span_6](end_span)
                regs(29) <= x"00003FFC"; -- $sp inicial = 0x3FFC[span_7](start_span)[span_7](end_span)[span_8](start_span)[span_8](end_span)
            else
                -- Escritura condicional (el registro $zero / $0 nunca se modifica)
                if we = '1' and to_integer(unsigned(wa)) /= 0 then
                    regs(to_integer(unsigned(wa))) <= wd;
                end if;
                -- Garantizar por seguridad que $zero permanezca en 0
                regs(0) <= (others => '0');
            end if;
        end if;
    end process;
end architecture rtl;
